// Logisim project Sequential_Circuit.circ as structural Verilog
module S_R_latch (
  input  S,
  input  R,
  input  clk,
  output Q,
  output Qn
);

  wire nand_1_out, nand_2_out;

  nand nand_1 (nand_1_out, S, clk);
  nand nand_2 (nand_2_out, clk, R);
  nand nand_3 (Q, nand_1_out, Qn);
  nand nand_4 (Qn, Q, nand_2_out);
endmodule

module D_flip_flop_pos_edge (
  input  d,
  input  clk,
  output q,
  output q_not
);

  wire not_1_out, not_2_out, s_r_latch_1_q, s_r_latch_1_qn;

  not not_1 (not_1_out, d);
  not not_2 (not_2_out, clk);
  S_R_latch s_r_latch_1 (.S(d), .R(not_1_out), .clk(not_2_out), .Q(s_r_latch_1_q), .Qn(s_r_latch_1_qn));
  S_R_latch s_r_latch_2 (.S(s_r_latch_1_q), .R(s_r_latch_1_qn), .clk(clk), .Q(q), .Qn(q_not));
endmodule

module D_flip_flop (
  input  d,
  input  reset,
  input  Clk,
  output Q,
  output not_Q
);

  wire and_1_out, not_1_out, not_2_out, s_r_latch_1_q, s_r_latch_1_qn;

  and and_1 (and_1_out, d, ~reset);  // AND_Gate
  not not_1 (not_1_out, Clk);
  not not_2 (not_2_out, and_1_out);
  S_R_latch s_r_latch_1 (.S(and_1_out), .R(not_2_out), .clk(not_1_out), .Q(s_r_latch_1_q), .Qn(s_r_latch_1_qn));
  S_R_latch s_r_latch_2 (.S(s_r_latch_1_q), .R(s_r_latch_1_qn), .clk(Clk), .Q(Q), .Qn(not_Q));
endmodule

module JK_Flip_Flop (
  input  J,
  input  Clk,
  input  K
);

  wire and_1_out, and_2_out, nand_1_out, nand_2_out;

  and and_1 (and_1_out, nand_2_out, J, Clk);
  and and_2 (and_2_out, Clk, K, nand_1_out);
  nand nand_1 (nand_1_out, and_1_out, nand_2_out);
  nand nand_2 (nand_2_out, nand_1_out, and_2_out);
  LED Q (.in(nand_1_out));
  LED Qbar (.in(nand_2_out));
endmodule

module Sequence_detector (
  input  Clk,
  input  X0,
  input  X1,
  input  Reset,
  output Z
);

  wire and_1_out, and_2_out, and_3_out, and_4_out, d_flip_flop_1_q, d_flip_flop_2_q;

  and and_1 (and_1_out, ~X0, X1, d_flip_flop_2_q);  // AND_Gate
  and and_2 (and_2_out, ~X0, ~X1);  // AND_Gate
  and and_3 (and_3_out, d_flip_flop_1_q, X1, X0);
  and and_4 (and_4_out, d_flip_flop_2_q, X1, X0);
  or or_1 (Z, and_3_out, and_4_out);
  D_flip_flop d_flip_flop_1 (.d(and_1_out), .reset(Reset), .Clk(Clk), .Q(d_flip_flop_1_q));  // open: not_Q
  D_flip_flop d_flip_flop_2 (.d(and_2_out), .reset(Reset), .Clk(Clk), .Q(d_flip_flop_2_q));  // open: not_Q
  LED led_1 (.in(d_flip_flop_1_q));
  LED led_2 (.in(d_flip_flop_2_q));

  // Notes on the sheet:
  //   D0
  //   D1
endmodule

module Multiplexer_3to1 (
  input  shift,
  input  load,
  input  a,
  input  b,
  input  c,
  output D_out
);

  wire and_1_out, and_2_out, and_3_out, not_1_out, not_2_out;

  not not_1 (not_1_out, shift);
  not not_2 (not_2_out, load);
  and and_1 (and_1_out, a, not_2_out, not_1_out);
  and and_2 (and_2_out, b, shift);
  or or_1 (D_out, and_1_out, and_2_out, and_3_out);
  and and_3 (and_3_out, c, not_1_out, load);
endmodule

module ShiftRegister_1bit (
  input  D0,
  input  S_in,
  input  D_in,
  input  shift,
  input  load,
  input  Clk,
  input  Reset,
  output out_8
);

  wire multiplexer_3to1_1_d_out;

  Multiplexer_3to1 multiplexer_3to1_1 (
    .shift(shift), .load(load), .a(D0), .b(S_in), .c(D_in), .D_out(multiplexer_3to1_1_d_out));
  D_flip_flop d_flip_flop_1 (.d(multiplexer_3to1_1_d_out), .reset(Reset), .Clk(Clk), .Q(out_8));  // open: not_Q
endmodule

module ShiftRegister_4bits (
  input  S_in,
  input  D0,
  input  D1,
  input  D2,
  input  D3,
  input  shift,
  input  Reset,
  input  load,
  input  Clock,
  output Q0,
  output Q1,
  output Q2,
  output Q3
);

  ShiftRegister_1bit shiftregister_1bit_1 (
    .D0(Q0), .S_in(S_in), .D_in(D0), .shift(shift), .load(load), .Clk(Clock), .Reset(Reset), .out_8(Q0));
  ShiftRegister_1bit shiftregister_1bit_2 (
    .D0(Q1), .S_in(Q0), .D_in(D1), .shift(shift), .load(load), .Clk(Clock), .Reset(Reset), .out_8(Q1));
  ShiftRegister_1bit shiftregister_1bit_3 (
    .D0(Q2), .S_in(Q1), .D_in(D2), .shift(shift), .load(load), .Clk(Clock), .Reset(Reset), .out_8(Q2));
  ShiftRegister_1bit shiftregister_1bit_4 (
    .D0(Q3), .S_in(Q2), .D_in(D3), .shift(shift), .load(load), .Clk(Clock), .Reset(Reset), .out_8(Q3));
endmodule

module Shift_Register_4bits_TEST (
  input  in_1,
  input  in_2,
  input  in_3,
  input  in_4,
  input  in_5,
  input  in_6,
  input  clk,
  input  reset,
  input  in_9,
  input  in_10,
  output out_11,
  output out_12,
  output out_13,
  output out_14
);

  wire multiplexer_1_out, multiplexer_2_out, multiplexer_3_out, multiplexer_4_out;

  Multiplexer #(.select(2)) multiplexer_1 (
    .in0(out_11), .in1(in_1), .in2(out_12), .in3(in_2), .out(multiplexer_1_out), .sel({in_9, in_10}));
  Multiplexer #(.select(2)) multiplexer_2 (
    .in0(out_12), .in1(out_11), .in2(out_13), .in3(in_3), .out(multiplexer_2_out), .sel({in_9, in_10}));
  Multiplexer #(.select(2)) multiplexer_3 (
    .in0(out_13), .in1(out_12), .in2(out_14), .in3(in_4), .out(multiplexer_3_out), .sel({in_9, in_10}));
  Multiplexer #(.select(2)) multiplexer_4 (
    .in0(out_14), .in1(out_13), .in2(in_5), .in3(in_6), .out(multiplexer_4_out), .sel({in_9, in_10}));
  D_Flip_Flop d_ff_1 (.D(multiplexer_1_out), .clk(clk), .Q(out_11), .reset(reset));  // open: Qn, preset
  D_Flip_Flop d_ff_2 (.D(multiplexer_2_out), .clk(clk), .Q(out_12), .reset(reset));  // open: Qn, preset
  D_Flip_Flop d_ff_3 (.D(multiplexer_3_out), .clk(clk), .Q(out_13), .reset(reset));  // open: Qn, preset
  D_Flip_Flop d_ff_4 (.D(multiplexer_4_out), .clk(clk), .Q(out_14), .reset(reset));  // open: Qn, preset
endmodule
